// Logisim project WBramki.circ as structural Verilog: 1 circuit, main circuit main
module main (
  input  in_1,
  input  in_2,
  input  in_3,
  input  in_4,
  input  in_5,
  input  in_6,
  input  in_7,
  input  in_8
);

  wire n7474_1_p2, n7474_1_p5, n7474_2_p2, n7474_2_p5, nand_1_out, nand_2_out, nand_3_out, nand_4_out,
       nand_5_out, nand_6_out, nand_7_out, not_1_out, not_2_out;

  not not_1 (not_1_out, in_1);
  not not_2 (not_2_out, in_5);
  nand nand_1 (nand_1_out, not_1_out, in_2, in_4);
  nand nand_2 (nand_2_out, in_1, in_3);
  nand nand_3 (nand_3_out, not_2_out, in_6, in_8);
  nand nand_4 (nand_4_out, in_5, in_7);
  nand nand_5 (nand_5_out, in_6, in_7, in_8);
  nand nand_6 (nand_6_out, nand_1_out, nand_2_out);
  LED led_1 (.in(n7474_1_p5));
  LED led_2 (.in(nand_6_out));
  nand nand_7 (nand_7_out, nand_3_out, nand_5_out, nand_4_out);
  LED led_3 (.in(nand_7_out));
  LED led_4 (.in(n7474_2_p5));
  // _7474 7474_1: pin names not known; wires that end beside it: 1'b0, n7474_1_p2, nand_6_out, 1'b0, n7474_1_p5, n7474_1_p2, 1'b0, 1'b1
  // _7474 7474_2: pin names not known; wires that end beside it: 1'b0, n7474_2_p2, nand_7_out, 1'b0, n7474_2_p5, n7474_2_p2, 1'b0, 1'b1
endmodule
