// Logisim project WHazard.circ as structural Verilog: 1 circuit, main circuit main
module main (
  input  a,
  input  b,
  input  c,
  input  d
);

  wire n7400_1_p9, n7400_1_p10, n7400_1_p17, n7400_1_p18, n7474_1_p3, n7474_1_p4, n7474_1_p6;

  // _7474 7474_1: pin names not known; wires that end beside it: 1'b1, 1'b1, n7474_1_p3, n7474_1_p4, 1'b0, n7474_1_p6, n7474_1_p3, 1'b0
  LED led_1 (.in(n7474_1_p4));
  // _7400 7400_1: pin names not known; wires that end beside it: 1'b0, n7474_1_p4, n7474_1_p3, n7474_1_p6, 1'b1, 1'b1, 1'b0, n7474_1_p6, n7400_1_p9, n7400_1_p10, n7400_1_p10, c, a, 1'b0, n7474_1_p6, n7400_1_p9, n7400_1_p17, n7400_1_p18, n7400_1_p10, d, c, b, a
  // _7404 7404_1: pin names not known; wires that end beside it: 1'b1, n7400_1_p17, d, n7400_1_p18, b, 1'b0, n7400_1_p9, n7400_1_p17
  // _7410 7410_1: pin names not known; wires that end beside it: 1'b0, n7474_1_p3, 1'b1, n7400_1_p18, a, 1'b0, n7400_1_p9, n7400_1_p17, n7400_1_p18, n7400_1_p10, d, c, b, a
  LED led_2 (.in(n7474_1_p6));
endmodule
