// Logisim project WUkłady — kopia.circ as structural Verilog: 1 circuit, main circuit main
module main (
  input  a,
  input  b,
  input  c,
  input  d
);

  wire n7400_1_p7, n7400_1_p8, n7400_1_p15, n7400_1_p16, n7400_1_p17, n7474_1_p3, n7474_1_p4, n7474_1_p6,
       not_2_out, not_3_out, not_4_out;

  LED led_1 (.in(n7474_1_p4));
  LED led_2 (.in(n7474_1_p6));
  // _7474 7474_1: pin names not known; wires that end beside it: 1'b1, 1'b1, n7474_1_p3, n7474_1_p4, 1'b0, n7474_1_p6, n7474_1_p3, 1'b0
  // _7400 7400_1: pin names not known; wires that end beside it: 1'b0, n7474_1_p3, 1'b1, 1'b1, 1'b0, n7474_1_p6, n7400_1_p7, n7400_1_p8, n7400_1_p8, c, a, 1'b0, n7400_1_p7, n7400_1_p8, n7400_1_p15, n7400_1_p16, n7400_1_p17, c, b, a
  // _7404 7404_1: pin names not known; wires that end beside it: 1'b1, n7400_1_p15, n7400_1_p17, n7400_1_p16, b, 1'b0, n7400_1_p7, n7400_1_p15
  // _7410 7410_1: pin names not known; wires that end beside it: 1'b0, n7474_1_p4, n7474_1_p3, n7474_1_p6, 1'b1, n7400_1_p16, a, 1'b0, n7474_1_p6, n7400_1_p7, n7400_1_p8, n7400_1_p15, n7400_1_p16, n7400_1_p17, c, b, a
  not not_1 (n7400_1_p17, not_2_out);
  not not_2 (not_2_out, not_3_out);
  not not_3 (not_3_out, not_4_out);
  not not_4 (not_4_out, d);

  // Notes on the sheet:
  //   LED 2
  //   LED 1
  //   2)
  //   0)
  //   1)
  //   3)
  //   0) NOT(a)
  //   1) NAND(a,c)
  //   2) NAND(NOT(a),b,c)
  //   3) NAND( NAND(a,c), NAND( a, NOT(b), NOT(d)))
endmodule
