// Logisim project WUkłady.circ as structural Verilog: 1 circuit, main circuit main
module main (
  input  a,
  input  a_2,
  input  b,
  input  b_2,
  input  c,
  input  c_2,
  input  d,
  input  d_2
);

  wire n7400_1_p4, n7400_1_p9, n7400_1_p13, n7400_1_p14, n7400_2_p9, n7400_2_p10, n7400_2_p17, n7400_2_p18,
       n7404_1_p4, n7474_1_p4, n7474_1_p5, n7474_1_p7, n7474_2_p3, n7474_2_p4, n7474_2_p6;

  // _7474 7474_1: pin names not known; wires that end beside it: 1'b1, 1'b1, 1'b0, n7474_1_p4, n7474_1_p5, 1'b0, n7474_1_p7, n7474_1_p4, 1'b0
  LED led_1 (.in(n7474_1_p5));
  LED led_2 (.in(n7474_1_p7));
  // _7400 7400_1: pin names not known; wires that end beside it: n7474_1_p5, n7474_1_p4, n7474_1_p7, n7400_1_p4, a_2, 1'b1, 1'b1, 1'b0, n7400_1_p9, c_2, a_2, 1'b0, n7400_1_p13, n7400_1_p14, d_2, c_2, b_2, a_2
  // _7404 7404_1: pin names not known; wires that end beside it: 1'b1, n7474_1_p7, n7400_1_p9, n7404_1_p4, n7400_1_p13, d_2, n7400_1_p14, b_2, 1'b0, n7404_1_p4, n7400_1_p13
  // _7410 7410_1: pin names not known; wires that end beside it: 1'b0, n7474_1_p4, n7400_1_p9, n7404_1_p4, n7400_1_p4, n7400_1_p4, n7400_1_p4, a_2, 1'b1, n7400_1_p14, a_2, c_2, b_2, 1'b0, n7404_1_p4, n7400_1_p13, n7400_1_p14, n7400_1_p9, d_2, c_2, b_2
  // _7474 7474_2: pin names not known; wires that end beside it: 1'b1, 1'b1, n7474_2_p3, n7474_2_p4, 1'b0, n7474_2_p6, n7474_2_p3, 1'b0
  LED led_3 (.in(n7474_2_p4));
  // _7400 7400_2: pin names not known; wires that end beside it: 1'b0, n7474_2_p4, n7474_2_p3, n7474_2_p6, 1'b1, 1'b1, 1'b0, n7474_2_p6, n7400_2_p9, n7400_2_p10, n7400_2_p10, c, a, 1'b0, n7474_2_p6, n7400_2_p9, n7400_2_p17, n7400_2_p18, n7400_2_p10, d, c, b, a
  // _7404 7404_2: pin names not known; wires that end beside it: 1'b1, n7400_2_p17, d, n7400_2_p18, b, 1'b0, n7400_2_p9, n7400_2_p17
  // _7410 7410_2: pin names not known; wires that end beside it: n7474_2_p3, 1'b1, n7400_2_p18, a, 1'b0, n7400_2_p9, n7400_2_p17, n7400_2_p18, n7400_2_p10, d, c, b, a
  LED led_4 (.in(n7474_2_p6));

  // Notes on the sheet:
  //   6)
  //   4)
  //   !d
  //   2)
  //   !b
  //   1)
  //   c
  //   a
  //   b
  //   d
  //   1) a !b !d
  //   2) !(ac)
  //   3) !(1 && 2)
  //   4) !(acd)
  //   6) 1 && 2 && 4
  //   !d
  //   1)
  //   c
  //   a
  //   2)
  //   d
  //   b
  //   !b
endmodule
