// Logisim project cw3-funkcja-na-bramkach.circ as structural Verilog: 1 circuit, main circuit main
module main (
  input  A,
  input  B,
  input  C,
  input  D
);

  wire n7474_1_p2, n7474_1_p5, n7474_2_p2, n7474_2_p5, nand_1_out, nand_2_out, nand_3_out, nand_4_out,
       nand_5_out, nand_6_out, nand_7_out, not_1_out, not_2_out, not_3_out, not_4_out;

  not not_1 (not_1_out, C);
  not not_2 (not_2_out, C);
  not not_3 (not_3_out, B);
  not not_4 (not_4_out, B);
  nand nand_1 (nand_1_out, A, not_3_out, D);
  nand nand_2 (nand_2_out, not_1_out, not_1_out, B);
  nand nand_3 (nand_3_out, A, not_4_out, D);
  nand nand_4 (nand_4_out, not_2_out, not_2_out, B);
  nand nand_5 (nand_5_out, A, not_2_out, D);
  nand nand_6 (nand_6_out, nand_1_out, nand_2_out);
  LED led_1 (.in(nand_6_out));
  nand nand_7 (nand_7_out, nand_3_out, nand_4_out, nand_5_out);
  LED led_2 (.in(nand_7_out));
  // _7474 7474_1: pin names not known; wires that end beside it: 1'b0, n7474_1_p2, nand_6_out, 1'b0, n7474_1_p5, n7474_1_p2, 1'b0, 1'b1
  LED led_3 (.in(n7474_1_p5));
  // _7474 7474_2: pin names not known; wires that end beside it: 1'b0, n7474_2_p2, nand_7_out, 1'b0, n7474_2_p5, n7474_2_p2, 1'b0, 1'b1
  LED led_4 (.in(n7474_2_p5));
endmodule
