// Logisim project cw3-funkcja-na-ukladach-z-hazardem.circ as structural Verilog: 1 circuit, main circuit main
module main (
  input  A,
  input  B,
  input  C,
  input  D,
  input  A_2,
  input  B_2,
  input  C_2,
  input  D_2
);

  wire n7400_1_p2, n7400_1_p3, n7400_1_p6, n7400_1_p7, n7400_2_p2, n7404_2_p1, n7404_2_p9, n7410_1_p4,
       n7410_2_p1, n7410_2_p7, n7410_2_p10, n7474_1_p1, n7474_1_p2, n7474_2_p1, n7474_2_p2;

  // _7400 7400_1: pin names not known; wires that end beside it: B, n7400_1_p2, n7400_1_p3, 1'b1, n7400_1_p3, n7400_1_p6, n7400_1_p7
  // _7410 7410_1: pin names not known; wires that end beside it: 1'b0, A, D, n7410_1_p4, n7400_1_p6, 1'b1
  // _7404 7404_1: pin names not known; wires that end beside it: 1'b0, B, n7410_1_p4, C, n7400_1_p2, 1'b0, 1'b1
  // _7400 7400_2: pin names not known; wires that end beside it: B_2, n7400_2_p2, 1'b1
  // _7410 7410_2: pin names not known; wires that end beside it: n7410_2_p1, 1'b0, A_2, n7400_2_p2, A_2, D_2, n7410_2_p7, 1'b1, D_2, n7410_2_p10, n7410_2_p10, n7410_2_p1
  // _7404 7404_2: pin names not known; wires that end beside it: n7404_2_p1, 1'b0, B_2, n7410_2_p7, C_2, n7400_2_p2, 1'b0, n7404_2_p1, n7404_2_p9, 1'b1
  LED led_1 (.in(n7400_1_p7));
  LED led_2 (.in(n7474_1_p2));
  LED led_3 (.in(n7474_2_p2));
  LED led_4 (.in(n7404_2_p9));
  // _7474 7474_1: pin names not known; wires that end beside it: n7474_1_p1, n7474_1_p2, 1'b0, n7400_1_p7, n7474_1_p1, 1'b0, 1'b1, 1'b0
  // _7474 7474_2: pin names not known; wires that end beside it: n7474_2_p1, n7474_2_p2, 1'b0, n7404_2_p9, n7474_2_p1, 1'b0, 1'b1, 1'b0
endmodule
